// Logisim project arithmetic circuit.circ as structural Verilog: 1 circuit, main circuit main
module main (
  input  A,
  input  B,
  input  A_2,
  input  B_2,
  input  C,
  input  IP_A,
  input  IP_B,
  input  IP_A_2,
  input  IP_B_2,
  input  IP_C,
  input  IP_A_3,
  input  IP_A_4,
  input  IP_B_3,
  input  IP_B_4,
  input  IP_A_5,
  input  IP_B_5,
  input  [1:0] AA,
  input  [3:0] AAAA,
  input  [1:0] BB,
  input  [3:0] BBBB,
  output Y,
  output Y_2,
  output Y_3,
  output Y_4,
  output Y_5,
  output Y_6,
  output OP_Y,
  output OP_Y_2,
  output OP_Y_3,
  output OP_Y_4,
  output OP_Y_5,
  output OP_Y_6,
  output Y_7,
  output Y_8,
  output Y_9,
  output Y_10,
  output Y_11,
  output Y_12
);

  wire and_2_out, and_3_out, and_4_out, and_6_out, and_7_out, and_8_out, and_10_out, and_11_out,
       comparator_2_eq, comparator_2_gt, comparator_2_lt, not_1_out, not_2_out, not_3_out, not_4_out,
       not_5_out, not_6_out, or_1_out, xor_2_out, xor_5_out;

  not not_1 (not_1_out, IP_A_2);
  not not_2 (not_2_out, IP_A);
  not not_3 (not_3_out, IP_A_4);
  Comparator #(.width(2)) comparator_1 (.a(AA), .b(BB), .gt(Y_10), .eq(Y_11), .lt(Y_12));
  xor xor_1 (Y, A, B);
  and and_1 (Y_2, A, B);
  xor xor_2 (xor_2_out, A_2, B_2);
  and and_2 (and_2_out, A_2, B_2);
  and and_3 (and_3_out, A_2, C);
  and and_4 (and_4_out, B_2, C);
  xor xor_3 (Y_5, IP_A, IP_B);
  and and_5 (Y_6, not_2_out, IP_B);
  not not_4 (not_4_out, IP_B_4);
  not not_5 (not_5_out, IP_A_5);
  not not_6 (not_6_out, IP_B_5);
  xor xor_4 (Y_3, xor_2_out, C);
  xor xor_5 (xor_5_out, IP_A_2, IP_B_2);
  and and_6 (and_6_out, not_1_out, IP_C);
  and and_7 (and_7_out, not_1_out, IP_B_2);
  and and_8 (and_8_out, IP_B_2, IP_C);
  and and_9 (OP_Y_3, IP_A_3, IP_A_4, IP_B_3, IP_B_4);
  or or_1 (or_1_out, not_3_out, not_4_out);
  and and_10 (and_10_out, IP_A_3, IP_B_4);
  and and_11 (and_11_out, IP_A_4, IP_B_3);
  and and_12 (OP_Y_6, IP_A_4, IP_B_4);
  and and_13 (Y_7, not_5_out, IP_B_5);
  and and_14 (Y_9, IP_A_5, not_6_out);
  or or_2 (Y_4, and_2_out, and_3_out, and_4_out);
  xor xor_6 (OP_Y, xor_5_out, IP_C);
  or or_3 (OP_Y_2, and_6_out, and_7_out, and_8_out);
  nor nor_1 (Y_8, Y_7, Y_9);
  Comparator #(.width(4)) comparator_2 (
    .a(AAAA), .b(BBBB), .gt(comparator_2_gt), .eq(comparator_2_eq), .lt(comparator_2_lt));
  and and_15 (OP_Y_4, or_1_out, IP_A_3, IP_B_3);
  xor xor_7 (OP_Y_5, and_10_out, and_11_out);
  DotMatrix #(.matrixcols(3), .matrixrows(1)) dotmatrix_1 (
    .col0(comparator_2_gt), .col1(comparator_2_eq), .col2(comparator_2_lt));

  // Notes on the sheet:
  //   2-BIT COMPARATOR
  //   HALF ADDER
  //   HALF SUBTRACTOR
  //   FULL ADDER
  //   MULTIPLIER
  //   SINGLE-BIT MAGNITUDE COMPARATOR
  //   FULL SUBTRACTOR
  //   4-BIT COMPARATOR
  //   YYY
endmodule
