// Logisim project code convertors.circ as structural Verilog: 1 circuit, main circuit main
module main (
  input  IP_B1,
  input  G1,
  input  IP_B2,
  input  G2,
  input  IP_B3,
  input  G3,
  input  IP_B4,
  input  G4,
  input  D1,
  input  D2,
  input  D1_2,
  input  D2_2,
  input  D3,
  input  D4,
  input  D3_2,
  input  D4_2,
  input  B1,
  input  B2,
  input  B3,
  input  B4,
  output G1_2,
  output B1_2,
  output G2_2,
  output B2_2,
  output G3_2,
  output B3_2,
  output G4_2,
  output B4_2,
  output G1_3,
  output G2_3,
  output G3_3,
  output G4_3,
  output E3,
  output E2,
  output E1,
  output E0,
  output D1_3,
  output D2_3,
  output D3_3,
  output D4_3,
  output D5
);

  wire and_2_out, and_3_out, and_6_out, and_7_out, and_8_out, not_1_out, not_2_out, not_3_out, not_4_out,
       not_5_out, or_2_out, or_3_out, or_5_out, or_6_out;

  or or_1 (G2_3, D1, D2);
  not not_1 (not_1_out, B1);
  not not_2 (not_2_out, B2);
  xor xor_1 (G2_2, IP_B1, IP_B2);
  xor xor_2 (G3_2, IP_B2, IP_B3);
  xor xor_3 (G4_2, IP_B3, IP_B4);
  xor xor_4 (G3_3, D2, D3_2);
  xor xor_5 (G4_3, D3_2, D4_2);
  not not_3 (not_3_out, B3);
  or or_2 (or_2_out, B2, B3);
  and and_1 (D2_3, B1, not_2_out, not_3_out);
  or or_3 (or_3_out, B1, B3);
  and and_2 (and_2_out, not_1_out, B3);
  and and_3 (and_3_out, B1, B2, not_3_out);
  xor xor_6 (B2_2, G1, G2);
  not not_4 (not_4_out, D3);
  not not_5 (not_5_out, D2_2);
  and and_4 (D1_3, or_2_out, B1);
  and and_5 (D3_3, or_3_out, B2);
  or or_4 (D4_3, and_2_out, and_3_out);
  not not_6 (E0, D4);
  xor xor_7 (B3_2, B2_2, G3);
  or or_5 (or_5_out, D4, D3);
  and and_6 (and_6_out, D2_2, not_4_out, E0);
  or or_6 (or_6_out, D4, D3);
  xor xor_8 (E1, D3, D4);
  and and_7 (and_7_out, or_5_out, D2_2);
  and and_8 (and_8_out, or_6_out, not_5_out);
  xor xor_9 (B4_2, B3_2, G4);
  or or_7 (E3, and_7_out, D1_2);
  or or_8 (E2, and_6_out, and_8_out);

  assign B1_2 = G1;
  assign D5 = B4;
  assign G1_2 = IP_B1;
  assign G1_3 = D1;

  // Notes on the sheet:
  //   BINARY TO GRAY CONVERSION
  //   BCD TO GRAY CONVERSION
  //   BINARY TO BCD CONVERSION
  //   GRAY TO BINARY CONVERSION
  //   BCD TO XS3 CONVERSION
endmodule
