// Logisim project combinational circuits.circ as structural Verilog: 1 circuit, main circuit main
module main (
  input  IP_A,
  input  IP_B,
  input  IP_A_2,
  input  IP_B_2,
  input  IP_A_3,
  input  IP_B_3,
  input  IP_C,
  input  IP_B_4,
  input  IP_C_2,
  input  in_10,
  input  IP_A_4,
  input  IP_B_5,
  input  IP_C_3,
  input  IP_A_5,
  input  IP_B_6,
  input  IP_C_4,
  input  IP_A_6,
  input  IP_A_7,
  input  IP_A_8,
  input  IP_B_7,
  input  IP_A_9,
  input  IP_B_8,
  output LHS,
  output RHS,
  output LHS_2,
  output RHS_2,
  output LHS_3,
  output RHS_3,
  output LHS_4,
  output RHS_4,
  output LHS_5,
  output RHS_5,
  output LHS_6,
  output RHS_6,
  output Y,
  output Y_2,
  output LHS_7,
  output LHS_8,
  output RHS_7,
  output RHS_8
);

  wire and_3_out, and_4_out, and_5_out, and_6_out, and_8_out, not_1_out, not_2_out, or_3_out, or_4_out,
       or_7_out, or_8_out, or_9_out;

  not not_1 (not_1_out, IP_A_6);
  or or_1 (LHS, IP_A, IP_B);
  or or_2 (RHS, IP_B, IP_A);
  and and_1 (LHS_2, IP_A_2, IP_B_2);
  and and_2 (RHS_2, IP_B_2, IP_A_2);
  or or_3 (or_3_out, IP_A_3, IP_A_3);
  and and_3 (and_3_out, IP_B_4, IP_C_2);
  or or_4 (or_4_out, IP_B_5, IP_C_3);
  and and_4 (and_4_out, IP_A_4, IP_B_5);
  and and_5 (and_5_out, IP_B_5, IP_A_4);
  or or_5 (Y_2, IP_A_6, not_1_out);
  nand nand_1 (LHS_7, IP_A_8, IP_B_7);
  or or_6 (RHS_7, ~IP_A_8, ~IP_B_7);  // OR_Gate
  or or_7 (or_7_out, IP_A_3, IP_A_3);
  and and_6 (and_6_out, IP_C_2, in_10);
  and and_7 (LHS_5, or_4_out, IP_A_4);
  and and_8 (and_8_out, IP_B_6, IP_C_4);
  or or_8 (or_8_out, IP_A_5, IP_B_6);
  or or_9 (or_9_out, IP_B_6, IP_A_5);
  or or_10 (LHS_3, or_3_out, IP_A_3);
  or or_11 (RHS_3, or_7_out, IP_A_3);
  and and_9 (LHS_4, and_3_out, in_10);
  and and_10 (RHS_4, and_6_out, in_10);
  or or_12 (RHS_5, and_4_out, and_5_out);
  not not_2 (not_2_out, IP_A_7);
  or or_13 (LHS_6, and_8_out, IP_A_5);
  and and_11 (RHS_6, or_8_out, or_9_out);
  and and_12 (Y, IP_A_7, not_2_out);
  nor nor_1 (LHS_8, IP_A_9, IP_B_8);
  and and_13 (RHS_8, ~IP_A_9, ~IP_B_8);  // AND_Gate

  assign IP_B_3 = IP_A_3;
  assign IP_C = IP_A_3;

  // Notes on the sheet:
  //   IP A
  //   NAND = BUBBLED OR GATE
  //   COMMUTATIVE LAW wrt +
  //   COMMUTATIVE LAW wrt *
  //   INVERSE LAW wrt +
  //   DEMORGAN'S LAW 
  //   ASSOCIATIVE LAW wrt +
  //   ASSOCIATIVE LAW wrt *
  //   DISTRIBUTIVE LAW wrt +
  //   DISTRIBUTIVE LAW wrt *
  //   INVERSE LAW wrt *
  //   NOR = BUBBLED AND GATE
  //   DEMORGANS LAW
endmodule
