// Logisim project counters.circ as structural Verilog: 1 circuit, main circuit main
module main (
);

  wire clock_1_out, clock_2_out, clock_3_out;
  wire [1:0] counter_1_q;
  wire [2:0] counter_3_q;
  wire [3:0] counter_2_q;

  Clock clock_1 (.out(clock_1_out));
  DotMatrix #(.matrixcols(1), .matrixrows(2)) dotmatrix_1 (.col0(counter_1_q));
  Counter #(.width(2), .max('h3)) counter_1 (.Q(counter_1_q), .clk(clock_1_out));  // open: load, D, count, carry, clr
  Clock clock_2 (.out(clock_2_out));
  Clock clock_3 (.out(clock_3_out));
  Hex_Digit_Display hex_digit_display_1 (.value(counter_2_q));  // open: dp
  Counter #(.width(4), .max('hf)) counter_2 (.Q(counter_2_q), .clk(clock_2_out));  // open: load, D, count, carry, clr
  Counter #(.width(3), .max('h7)) counter_3 (.Q(counter_3_q), .clk(clock_3_out));  // open: load, D, count, carry, clr
  DotMatrix #(.matrixcols(1), .matrixrows(3)) dotmatrix_2 (.col0(counter_3_q));

  // Notes on the sheet:
  //   2-BIT COUNTER
  //   4-BIT COUNTER
  //   3-BIT COUNTER
endmodule
