// Logisim project encoder and decoder circuit.circ as structural Verilog: 1 circuit, main circuit main
module main (
  input  in_1,
  input  in_2,
  input  in_3,
  input  in_4,
  input  in_5,
  input  in_6,
  input  in_7,
  input  in_8,
  input  in_9,
  input  in_10,
  input  [1:0] _2_4_DECODER,
  input  in_12,
  input  in_13,
  input  in_14,
  input  in_15,
  input  in_16,
  input  [2:0] in_17,
  input  in_18,
  input  in_19,
  input  in_20,
  input  in_21,
  input  in_22,
  input  in_23,
  input  in_24,
  input  in_25,
  input  in_26,
  output out_27,
  output out_28,
  output out_29,
  output out_30,
  output out_31,
  output out_32,
  output out_33,
  output out_34,
  output out_35,
  output out_36,
  output out_37,
  output out_38,
  output out_39,
  output out_40,
  output out_41,
  output out_42,
  output out_43,
  output out_44,
  output out_45,
  output out_46,
  output out_47,
  output out_48,
  output out_49,
  output out_50,
  output out_51,
  output out_52,
  output out_53,
  output out_54
);

  wire not_1_out, not_2_out, not_3_out, not_4_out, not_5_out, not_6_out, priority_encoder_1_gs;
  wire [1:0] priority_encoder_2_out;
  wire [2:0] priority_encoder_3_out;

  not not_1 (not_1_out, in_5);
  not not_2 (not_2_out, in_7);
  not not_3 (not_3_out, in_8);
  not not_4 (not_4_out, in_9);
  and and_1 (out_27, in_4, not_1_out);
  and and_2 (out_29, in_4, in_5);
  and and_3 (out_33, in_6, not_2_out, not_3_out, not_4_out);
  and and_4 (out_34, in_6, not_2_out, not_3_out, in_9);
  and and_5 (out_35, in_6, not_2_out, in_8, not_4_out);
  and and_6 (out_36, in_6, not_2_out, in_8, in_9);
  and and_7 (out_37, in_6, in_7, not_3_out, not_4_out);
  and and_8 (out_40, in_6, in_7, not_3_out, in_9);
  and and_9 (out_41, in_6, in_7, in_8, not_4_out);
  and and_10 (out_42, in_6, in_7, in_8, in_9);
  Decoder #(.select(3)) decoder_1 (
    .out0(out_47), .out1(out_48), .out2(out_49), .out3(out_50), .out4(out_51), .out5(out_52), .out6(out_53),
    .out7(out_54), .sel(in_17));  // open: en
  not not_5 (not_5_out, in_2);
  not not_6 (not_6_out, in_3);
  and and_11 (out_28, in_1, not_5_out, not_6_out);
  and and_12 (out_30, in_1, not_5_out, in_3);
  and and_13 (out_31, in_1, in_2, not_6_out);
  and and_14 (out_32, in_1, in_2, in_3);
  Decoder decoder_2 (.out0(out_38), .out1(out_39), .sel(in_10));  // open: en
  Decoder #(.select(2)) decoder_3 (
    .out0(out_43), .out1(out_44), .out2(out_45), .out3(out_46), .sel(_2_4_DECODER));  // open: en
  DotMatrix #(.matrixcols(1), .matrixrows(1)) dotmatrix_1 (.col0(priority_encoder_1_gs));
  Priority_Encoder #(.select(1)) priority_encoder_1 (
    .in0(in_12), .in1(in_13), .gs(priority_encoder_1_gs));  // open: out, en_out, en_in
  DotMatrix #(.matrixcols(1), .matrixrows(2)) dotmatrix_2 (.col0(priority_encoder_2_out));
  Priority_Encoder #(.select(2)) priority_encoder_2 (
    .in0(in_14), .in1(in_15), .in2(in_16), .in3(in_18), .out(priority_encoder_2_out));  // open: gs, en_out, en_in
  DotMatrix #(.matrixcols(1), .matrixrows(3)) dotmatrix_3 (.col0(priority_encoder_3_out));
  Priority_Encoder priority_encoder_3 (
    .in0(in_19), .in1(in_20), .in2(in_21), .in3(in_22), .in4(in_23), .in5(in_24), .in6(in_25), .in7(in_26),
    .out(priority_encoder_3_out));  // open: en_in, gs, en_out

  // Notes on the sheet:
  //   3:8 DECODER
  //   3:8 DECODER
  //   1:2 DECODER
  //   2:4 DECODER
  //   2:1 PRIORITY ENCODER
  //   8:3 PRIORITY ENCODER
  //   1:2 DECODER
  //   4:2 PRIORITY ENCODER
endmodule
