// Logisim project flip-flop.circ as structural Verilog: 1 circuit, main circuit main
module main (
  input  in_1,
  input  in_2,
  input  in_3,
  input  in_4,
  input  in_5,
  input  in_6,
  input  in_7,
  input  in_8,
  input  in_9,
  input  in_10,
  input  in_11,
  input  in_12,
  input  in_13,
  input  in_14,
  input  in_15,
  input  in_16,
  input  in_17,
  input  in_18,
  output out_19,
  output out_20,
  output out_21,
  output out_22,
  output out_23,
  output out_24,
  output out_25,
  output out_26,
  output out_27,
  output out_28,
  output out_29,
  output out_30,
  output out_31,
  output out_32,
  output out_33,
  output out_34,
  output out_35,
  output out_36,
  output out_37,
  output out_38,
  output out_39,
  output out_40,
  output out_41,
  output out_42
);

  wire clock_1_out, clock_2_out, clock_3_out, clock_4_out, clock_5_out, clock_6_out, clock_7_out,
       clock_8_out, clock_9_out, clock_10_out, clock_11_out, clock_12_out, d_ff_1_q, d_ff_1_qn, d_ff_2_q,
       d_ff_2_qn, d_ff_3_q, d_ff_3_qn, d_ff_4_q, d_ff_4_qn, j_k_ff_1_q, j_k_ff_1_qn, j_k_ff_2_q, j_k_ff_2_qn,
       s_r_ff_1_q, s_r_ff_1_qn, s_r_ff_2_q, s_r_ff_2_qn, s_r_ff_3_q, s_r_ff_3_qn, s_r_ff_4_q, s_r_ff_4_qn,
       t_ff_1_q, t_ff_1_qn, t_ff_2_q, t_ff_2_qn, undriven, undriven_2, undriven_3, undriven_4, undriven_5,
       undriven_6, undriven_7, undriven_8, undriven_9, undriven_10, undriven_11, undriven_12, undriven_13,
       undriven_14, undriven_15, undriven_16, undriven_17, undriven_18, undriven_19, undriven_20,
       undriven_21, undriven_22, undriven_23, undriven_24, undriven_25, undriven_26, undriven_27,
       undriven_28, undriven_29, undriven_30;

  S_R_Flip_Flop s_r_ff_1 (
    .S(undriven), .clk(undriven_2), .R(undriven_3), .Q(s_r_ff_1_q), .Qn(s_r_ff_1_qn));  // open: preset, reset, en
  S_R_Flip_Flop s_r_ff_2 (
    .S(undriven_12), .clk(undriven_13), .R(undriven_14), .Q(s_r_ff_2_q), .Qn(s_r_ff_2_qn));  // open: preset, reset, en
  S_R_Flip_Flop s_r_ff_3 (
    .S(undriven_18), .clk(undriven_19), .R(undriven_20), .Q(s_r_ff_3_q), .Qn(s_r_ff_3_qn));  // open: preset, reset, en
  S_R_Flip_Flop s_r_ff_4 (
    .S(undriven_15), .clk(undriven_16), .R(undriven_17), .Q(s_r_ff_4_q), .Qn(s_r_ff_4_qn));  // open: preset, reset, en
  D_Flip_Flop d_ff_1 (.clk(undriven_4), .D(undriven_5), .Q(d_ff_1_q), .Qn(d_ff_1_qn));  // open: preset, en, reset
  D_Flip_Flop d_ff_2 (.clk(undriven_6), .D(undriven_7), .Q(d_ff_2_q), .Qn(d_ff_2_qn));  // open: preset, en, reset
  D_Flip_Flop d_ff_3 (.clk(undriven_8), .D(undriven_9), .Q(d_ff_3_q), .Qn(d_ff_3_qn));  // open: preset, en, reset
  D_Flip_Flop d_ff_4 (.clk(undriven_10), .D(undriven_11), .Q(d_ff_4_q), .Qn(d_ff_4_qn));  // open: preset, en, reset
  J_K_Flip_Flop j_k_ff_1 (
    .J(undriven_24), .clk(undriven_25), .K(undriven_26), .Q(j_k_ff_1_q), .Qn(j_k_ff_1_qn));  // open: preset, en, reset
  J_K_Flip_Flop j_k_ff_2 (
    .J(undriven_21), .clk(undriven_22), .K(undriven_23), .Q(j_k_ff_2_q), .Qn(j_k_ff_2_qn));  // open: preset, en, reset
  T_Flip_Flop t_ff_1 (.clk(undriven_29), .T(undriven_30), .Q(t_ff_1_q), .Qn(t_ff_1_qn));  // open: preset, reset, en
  T_Flip_Flop t_ff_2 (.clk(undriven_27), .T(undriven_28), .Q(t_ff_2_q), .Qn(t_ff_2_qn));  // open: preset, reset, en
  Clock clock_1 (.out(clock_1_out));
  Clock clock_2 (.out(clock_2_out));
  Clock clock_3 (.out(clock_3_out));
  Clock clock_4 (.out(clock_4_out));
  S_R_Flip_Flop s_r_ff_5 (.S(in_1), .clk(clock_1_out), .R(in_2), .Q(out_19), .Qn(out_20));  // open: preset, reset, en
  S_R_Flip_Flop #(.trigger("falling")) s_r_ff_6 (
    .S(in_3), .clk(clock_2_out), .R(in_4), .Q(out_21), .Qn(out_22));  // open: preset, reset, en
  S_R_Flip_Flop #(.trigger("high")) s_r_ff_7 (
    .S(in_5), .clk(clock_3_out), .R(in_6), .Q(out_23), .Qn(out_24));  // open: preset, reset, en
  S_R_Flip_Flop #(.trigger("low")) s_r_ff_8 (
    .S(in_7), .clk(clock_4_out), .R(in_8), .Q(out_25), .Qn(out_26));  // open: preset, reset, en
  Clock clock_5 (.out(clock_5_out));
  Clock clock_6 (.out(clock_6_out));
  Clock clock_7 (.out(clock_7_out));
  Clock clock_8 (.out(clock_8_out));
  Clock clock_9 (.out(clock_9_out));
  Clock clock_10 (.out(clock_10_out));
  Clock clock_11 (.out(clock_11_out));
  Clock clock_12 (.out(clock_12_out));
  D_Flip_Flop d_ff_5 (.clk(in_9), .D(clock_5_out), .Q(out_27), .Qn(out_28));  // open: preset, en, reset
  D_Flip_Flop #(.trigger("falling")) d_ff_6 (
    .clk(in_10), .D(clock_6_out), .Q(out_29), .Qn(out_30));  // open: preset, en, reset
  D_Flip_Flop #(.trigger("high")) d_ff_7 (
    .clk(in_11), .D(clock_7_out), .Q(out_31), .Qn(out_32));  // open: preset, en, reset
  D_Flip_Flop #(.trigger("low")) d_ff_8 (
    .clk(in_12), .D(clock_8_out), .Q(out_33), .Qn(out_34));  // open: preset, en, reset
  J_K_Flip_Flop j_k_ff_3 (.J(in_13), .clk(clock_9_out), .K(in_14), .Q(out_35), .Qn(out_36));  // open: preset, en, reset
  J_K_Flip_Flop #(.trigger("falling")) j_k_ff_4 (
    .J(in_15), .clk(clock_10_out), .K(in_16), .Q(out_37), .Qn(out_38));  // open: preset, en, reset
  T_Flip_Flop t_ff_3 (.clk(in_17), .T(clock_11_out), .Q(out_39), .Qn(out_40));  // open: preset, reset, en
  T_Flip_Flop #(.trigger("falling")) t_ff_4 (
    .clk(in_18), .T(clock_12_out), .Q(out_41), .Qn(out_42));  // open: preset, reset, en

  // Notes on the sheet:
  //   SR FLIP FLOP
  //   SR FLIP FLOP
  //   SR FLIP FLOP
  //   SR FLIP FLOP
  //   D FLIP FLOP
  //   D FLIP FLOP
  //   D FLIP FLOP
  //   D FLIP FLOP
  //   JK FLIP FLOP
  //   JK FLIP FLOP
  //   T FLIP FLOP
  //   T FLIP FLOP
  //   [POSITIVE] RISING EDGE
  //   [NEGATIVE] FALLING EDGE
  //   HIGH LEVEL
  //   LOW LEVEL
  //   [POSITIVE] RISING EDGE
  //   [NEGATIVE] FALLING EDGE
  //   HIGH LEVEL
  //   LOW LEVEL
  //   [POSITIVE] RISING EDGE
  //   [NEGATIVE] FALLING EDGE
  //   [POSITIVE] RISING EDGE
  //   [NEGATIVE] FALLING EDGE
endmodule
