// Logisim project multiplexer and demultiplexer.circ as structural Verilog: 1 circuit, main circuit main
module main (
  input  E,
  input  S,
  input  D0,
  input  D1,
  input  E_2,
  input  S_2,
  input  S_3,
  input  A,
  input  A_2,
  input  B,
  input  B_2,
  input  D0_2,
  input  in_13,
  input  D0_3,
  input  in_15,
  input  D1_2,
  input  D3,
  input  in_18,
  input  [1:0] in_19,
  input  D0_4,
  input  D0_5,
  input  in_22,
  input  in_23,
  input  in_24,
  input  in_25,
  input  in_26,
  input  in_27,
  input  in_28,
  input  in_29,
  input  in_30,
  input  OP_Y,
  input  D7,
  input  in_33,
  input  in_34,
  input  in_35,
  input  [2:0] in_36,
  input  in_37,
  input  in_38,
  input  in_39,
  input  in_40,
  input  in_41,
  input  in_42,
  input  in_43,
  input  in_44,
  input  D15,
  input  in_46,
  input  [3:0] in_47,
  input  in_48,
  input  in_49,
  input  in_50,
  input  in_51,
  input  in_52,
  input  in_53,
  input  in_54,
  input  S_4,
  input  IP,
  input  in_57,
  input  [1:0] SS,
  input  IP_2,
  input  [2:0] SSS,
  input  IP_3,
  input  [3:0] SSSS,
  output Y,
  output Y_2,
  output OP_Y_2,
  output OP_Y_3,
  output out_67,
  output OP_Y_4,
  output out_69,
  output out_70,
  output out_71,
  output out_72,
  output out_73,
  output out_74,
  output Y0,
  output out_76,
  output Y0_2,
  output Y1,
  output Y3,
  output out_80,
  output Y0_3,
  output out_82,
  output out_83,
  output out_84,
  output out_85,
  output out_86,
  output Y7,
  output out_88,
  output Y0_4,
  output out_90,
  output out_91,
  output out_92,
  output out_93,
  output out_94,
  output out_95,
  output out_96,
  output out_97,
  output out_98,
  output out_99,
  output out_100,
  output out_101,
  output out_102,
  output Y15,
  output out_104
);

  wire and_3_out, and_4_out, and_5_out, and_6_out, and_7_out, and_8_out, not_1_out, not_3_out, not_4_out,
       not_5_out, not_6_out, not_7_out;

  not not_1 (not_1_out, S);
  // NOT_Gate not_2 is placed but not wired
  not not_3 (not_3_out, in_49);
  Demultiplexer demultiplexer_1 (.out0(Y0_2), .out1(Y1), .in(S_4), .sel(in_57));  // open: en
  Demultiplexer #(.select(3)) demultiplexer_2 (
    .out0(Y0_3), .out1(out_82), .out2(out_83), .out3(out_84), .out4(out_85), .out5(out_86), .out6(Y7),
    .out7(out_88), .in(IP_2), .sel(SSS));  // open: en
  not not_4 (not_4_out, S_3);
  not not_5 (not_5_out, S_2);
  Multiplexer multiplexer_1 (.in0(D0_3), .in1(D1_2), .out(OP_Y_3), .sel(in_18));  // open: en
  Multiplexer #(.select(3)) multiplexer_2 (
    .in0(D0_4), .in1(in_22), .in2(in_24), .in3(in_26), .in4(in_28), .in5(in_30), .in6(D7), .in7(in_34),
    .out(out_67), .sel(in_36));  // open: en
  and and_1 (out_69, in_48, not_3_out, in_50);
  and and_2 (out_71, in_48, in_49, in_50);
  and and_3 (and_3_out, E, not_1_out, D0);
  and and_4 (and_4_out, E, S, D1);
  and and_5 (and_5_out, E_2, not_5_out, not_4_out, A);
  and and_6 (and_6_out, E_2, not_5_out, S_3, A_2);
  and and_7 (and_7_out, E_2, S_2, not_4_out, B);
  and and_8 (and_8_out, E_2, S_2, S_3, B_2);
  or or_1 (Y, and_3_out, and_4_out);
  Multiplexer #(.select(2)) multiplexer_3 (
    .in0(D0_2), .in1(in_13), .in2(in_15), .in3(D3), .out(OP_Y_2), .sel(in_19));  // open: en
  Demultiplexer #(.select(4)) demultiplexer_3 (
    .out0(Y0_4), .out1(out_90), .out2(out_91), .out3(out_92), .out4(out_93), .out5(out_94), .out6(out_95),
    .out7(out_96), .out8(out_97), .out9(out_98), .out10(out_99), .out11(out_100), .out12(out_101),
    .out13(out_102), .out14(Y15), .out15(out_104), .in(IP_3), .sel(SSSS));  // open: en
  or or_2 (Y_2, and_5_out, and_6_out, and_7_out, and_8_out);
  Multiplexer #(.select(4)) multiplexer_4 (
    .in0(D0_5), .in1(in_23), .in2(in_25), .in3(in_27), .in4(in_29), .in5(OP_Y), .in6(in_33), .in7(in_35),
    .in8(in_37), .in9(in_38), .in10(in_39), .in11(in_40), .in12(in_41), .in13(in_44), .in14(D15),
    .in15(in_46), .out(OP_Y_4), .sel(in_47));  // open: en
  not not_6 (not_6_out, in_52);
  not not_7 (not_7_out, in_53);
  Demultiplexer #(.select(2)) demultiplexer_4 (
    .out0(Y0), .out1(out_76), .out2(Y3), .out3(out_80), .in(IP), .sel(SS));  // open: en
  and and_9 (out_70, in_51, not_6_out, not_7_out, in_54);
  and and_10 (out_72, in_51, not_6_out, in_53, in_54);
  and and_11 (out_73, in_51, in_52, not_7_out, in_54);
  and and_12 (out_74, in_51, in_52, in_53, in_54);

  // Notes on the sheet:
  //   IP
  //   2:1 MULTIPLEXER by using ICS
  //   8:1 MULTIPLEXER by using ICS
  //   2;1 DE MULTIPLEXER
  //   8:1 DE MULTIPLEXER
  //   2:1 MULTIPLEXER
  //   4:1 MULTIPLEXER
  //   16:1 MULTIPLEXER by using ICS
  //   16:1 DE MULTIPLEXER
  //   4:1 MULTIPLEXER by using ICS
  //   4:1 DE MULTIPLEXER
endmodule
