// Logisim project study of logic gates.circ as structural Verilog: 1 circuit, main circuit main
module main (
  input  IP_A,
  input  IP_A_2,
  input  IP_B,
  input  IP_A_3,
  input  IP_A_4,
  input  IP_A_5,
  input  IP_B_2,
  input  IP_B_3,
  input  IP_A_6,
  input  IP_B_4,
  input  IP_A_7,
  input  IP_A_8,
  input  IP_B_5,
  input  IP_B_6,
  input  IP_C,
  input  IP_C_2,
  input  IP_A_9,
  input  IP_A_10,
  input  IP_B_7,
  input  IP_B_8,
  input  IP_A_11,
  input  IP_A_12,
  input  IP_B_9,
  input  IP_B_10,
  input  IP_A_13,
  input  IP_A_14,
  input  IP_B_11,
  input  IP_B_12,
  input  IP_C_3,
  input  IP_C_4,
  input  IP_A_15,
  input  IP_A_16,
  input  IP_B_13,
  input  IP_B_14,
  input  IP_A_17,
  input  IP_A_18,
  input  IP_B_15,
  input  IP_B_16,
  input  IP_A_19,
  input  IP_A_20,
  input  IP_B_17,
  input  IP_B_18,
  input  IP_C_5,
  input  IP_C_6,
  output OP_Y,
  output OP_Y_2,
  output OP_Y_3,
  output OP_Y_4,
  output OP_Y_5,
  output OP_Y_6,
  output OP_Y_7,
  output OP_Y_8,
  output OP_Y_9,
  output OP_Y_10,
  output OP_Y_11,
  output OPY,
  output OP_Y_12,
  output OP_Y_13,
  output OP_Y_14,
  output OP_Y_15,
  output OP_Y_16,
  output OP_Y_17,
  output OP_Y_18,
  output OP_Y_19
);

  not not_1 (OP_Y, IP_A_2);
  not not_2 (OP_Y_3, IP_A_3);
  nand nand_1 (OP_Y_10, IP_A_10, IP_B_8);
  nand nand_2 (OPY, IP_A_12, IP_B_10);
  nand nand_3 (OP_Y_13, IP_A_14, IP_B_12, IP_C_4);
  xor xor_1 (OP_Y_14, IP_A_15, IP_B_13);
  xor xor_2 (OP_Y_16, IP_A_17, IP_B_15);
  ExactlyOne xor_3 (.out(OP_Y_18), .in1(IP_A_19), .in2(IP_B_17), .in3(IP_C_5));
  and and_1 (OP_Y_4, IP_A_4, IP_B_2);
  and and_2 (OP_Y_6, IP_A_6, IP_B_4);
  and and_3 (OP_Y_8, IP_A_8, IP_B_6, IP_C_2);
  or or_1 (OP_Y_2, IP_A, IP_B);
  or or_2 (OP_Y_5, IP_A_5, IP_B_3);
  or or_3 (OP_Y_7, IP_A_7, IP_B_5, IP_C);
  nor nor_1 (OP_Y_9, IP_A_9, IP_B_7);
  nor nor_2 (OP_Y_11, IP_A_11, IP_B_9);
  nor nor_3 (OP_Y_12, IP_A_13, IP_B_11, IP_C_3);
  xnor xnor_1 (OP_Y_15, IP_A_16, IP_B_14);
  xnor xnor_2 (OP_Y_17, IP_A_18, IP_B_16);
  NotExactlyOne xnor_3 (.out(OP_Y_19), .in1(IP_A_20), .in2(IP_B_18), .in3(IP_C_6));

  // Notes on the sheet:
  //   NOT GATE
  //   NOT GATE
  //   AND GATE
  //   2-IP AND GATE
  //   3-IP AND GATE
  //   NAND GATE
  //   2-IP NAND GATE
  //   3-IP NAND GATE
  //   XOR GATE
  //   2-IP XOR GATE
  //   3-IP XOR GATE
  //   OR GATE
  //   2-IP OR GATE
  //   3-IP OR GATE
  //   NOR GATE
  //   2-IP NOR GATE
  //   3-IP NOR GATE
  //   XNOR GATE
  //   2-IP XNOR GATE
  //   3-IP XNOR GATE
endmodule
