// Logisim project universality of nand and nor gates.circ as structural Verilog: 1 circuit, main circuit main
module main (
  input  IP_A,
  input  IP_A_2,
  input  IP_A_3,
  input  IP_B,
  input  IP_A_4,
  input  IP_A_5,
  input  IP_B_2,
  input  IP_B_3,
  input  IP_A_6,
  input  IP_A_7,
  input  IP_B_4,
  input  IP_B_5,
  input  IP_A_8,
  input  IP_A_9,
  input  IP_B_6,
  input  IP_B_7,
  input  IP_A_10,
  input  IP_A_11,
  input  IP_B_8,
  input  IP_B_9,
  input  IP_A_12,
  input  IP_B_10,
  output OP_Y,
  output OP_Y_2,
  output OP_Y_3,
  output OP_Y_4,
  output OP_Y_5,
  output OP_Y_6,
  output OP_Y_7,
  output OP_Y_8,
  output OP_Y_9,
  output OP_Y_10,
  output OP_Y_11,
  output OP_Y_12
);

  wire and_1_out, and_2_out, and_3_out, and_4_out, nand_2_out, nand_3_out, nand_4_out, nand_5_out,
       nand_6_out, nand_7_out, nand_8_out, nand_11_out, nand_12_out, nand_13_out, nor_2_out, nor_3_out,
       nor_4_out, nor_6_out, nor_7_out, nor_8_out, nor_9_out, nor_10_out, nor_12_out, nor_13_out, nor_14_out,
       nor_15_out, nor_16_out;

  buf and_1 (and_1_out, IP_A_11);  // AND_Gate
  nand nand_1 (OP_Y, IP_A, IP_A);
  nand nand_2 (nand_2_out, IP_A_3, IP_B);
  nand nand_3 (nand_3_out, IP_A_5, IP_A_5);
  nand nand_4 (nand_4_out, IP_B_3, IP_B_3);
  not nand_5 (nand_5_out, IP_A_7);  // NAND_Gate
  not nand_6 (nand_6_out, IP_B_5);  // NAND_Gate
  nand nand_7 (nand_7_out, IP_A_9, IP_A_9);
  nand nand_8 (nand_8_out, IP_B_7, IP_B_7);
  buf and_2 (and_2_out, IP_B_9);  // AND_Gate
  nand nand_9 (OP_Y_3, nand_2_out, nand_2_out);
  nand nand_10 (OP_Y_5, nand_3_out, nand_4_out);
  nand nand_11 (nand_11_out, nand_5_out, nand_6_out);
  nand nand_12 (nand_12_out, nand_7_out, IP_B_7);
  nand nand_13 (nand_13_out, nand_8_out, IP_A_9);
  and and_3 (and_3_out, IP_A_11, IP_B_9);
  and and_4 (and_4_out, and_2_out, and_1_out);
  nand nand_14 (OP_Y_9, nand_12_out, nand_13_out);
  and and_5 (OP_Y_11, and_3_out, and_4_out);
  nand nand_15 (OP_Y_7, nand_11_out, nand_11_out);
  nor nor_1 (OP_Y_2, IP_A_2, IP_A_2);
  nor nor_2 (nor_2_out, IP_A_4, IP_A_4);
  nor nor_3 (nor_3_out, IP_B_2, IP_B_2);
  nor nor_4 (nor_4_out, IP_A_6, IP_B_4);
  nor nor_5 (OP_Y_4, nor_2_out, nor_3_out);
  nor nor_6 (nor_6_out, IP_A_8, IP_A_8);
  nor nor_7 (nor_7_out, IP_B_6, IP_B_6);
  nor nor_8 (nor_8_out, IP_A_10, IP_A_10);
  nor nor_9 (nor_9_out, IP_B_8, IP_B_8);
  nor nor_10 (nor_10_out, IP_A_12, IP_B_10);
  nor nor_11 (OP_Y_6, nor_4_out, nor_4_out);
  nor nor_12 (nor_12_out, nor_6_out, nor_7_out);
  nor nor_13 (nor_13_out, IP_B_8, IP_A_10);
  nor nor_14 (nor_14_out, IP_A_12, nor_10_out);
  nor nor_15 (nor_15_out, nor_10_out, IP_B_10);
  nor nor_16 (nor_16_out, nor_8_out, nor_9_out);
  nor nor_17 (OP_Y_8, nor_12_out, nor_12_out);
  nor nor_18 (OP_Y_10, nor_16_out, nor_13_out);
  nor nor_19 (OP_Y_12, nor_14_out, nor_15_out);

  // Notes on the sheet:
  //   NOT GATE by using NAND GATE
  //   AND GATE by using NAND GATE
  //   OR GATE by using NAND GATE
  //   NOR GATE by using NAND GATE
  //   XOR GATE by using NAND GATE
  //   XNOR GATE by using NAND GATE
  //   NOT GATE by using NOR GATE
  //   AND GATE by using NOR GATE
  //   OR GATE by using NOR GATE
  //   NAND GATE by using NOR GATE
  //   XOR GATE by using NOR GATE
  //   XNOR GATE by using NOR GATE
endmodule
